# Fritzing sketch ClearAir (saved by Fritzing 0.9.6b)
circuit board: 8.46667cm x 5.64444cm

parts:
  Feather_M0_WiFi = Adafruit Feather M0 WINC1500 [part_number="Adafruit #3010"]
  PMSA003I = Adafruit PMSA003I Air Quality Breakout [part_number="Adafruit #4632"]
  BME680 = Adafruit BME680

nets:
  GND: Feather_M0_WiFi.GND, PMSA003I.GND, BME680.GND
  3.3V: Feather_M0_WiFi.+3V3, PMSA003I.3.3V, BME680.3.3V
  N1: Feather_M0_WiFi.SCL, PMSA003I.SCL, BME680.SCK/SCL
  N2: Feather_M0_WiFi.SDA, PMSA003I.SDA, BME680.SDI/SDA

custom parts:
  Adafruit Feather M0 WINC1500: This is the Adafruit Feather M0 WiFi w/ATWINC1500 - our take on an 'all-in-one' Arduino-compatible + high speed, reliable WiFi with built in USB and battery charging. Its an Adafruit Feather M0 with a WiFi module, ready to rock! Connect your Feather to the Internet with this fine new FCC-certified WiFi module from Atmel. This 802.11bgn-capable WiFi module is the best new thing for networking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
  Adafruit PMSA003I Air Quality Breakout: Breathe easy, knowing that you can track and sense the quality of the air around you with this Adafruit PMSA003I Air Quality Breakout. This sensor is great for monitoring air quality, in a compact plug-in format. Best of all, unlike almost all other sensors we've seen that are UART interface, this one is I2C interface, which makes it a great match for single board Linux computers like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
